# Fritzing sketch Untitled Sketch 2 (saved by Fritzing 0.9.3b)

parts:
  SensorShield3 = Duit connection plate [package="5 mm [THT]"]
  SensorShield2 = Duit connection plate [package="5 mm [THT]"]
  SensorShield1 = Duit connection plate [package="5 mm [THT]"]
  U1 = Sensor_shield_DUIT
  U2 = Sensor_shield_DUIT
  U3 = Sensor_shield_DUIT
  LCD1 = LCD screen 1602
  LCM1602_IIC1 = I2C [part_number="LCM1602 IIC" chip_label="LCM1602 IIC" package="DIP (Dual Inline) [THT]"]
  Деталь1 = Arduino Nano (Rev3.0)
  Деталь2 = Arduino Nano (Rev3.0)
  Деталь3 = Arduino Nano (Rev3.0)
  YL-83_-_Control_Board1 = YL-83 Rain Sensor - Control Board
  YL-83_-_Detection_Board1 = YL-83 Rain Sensor - Detection Board
  M1 = 1 chan 5v relay module
  M2 = hcmmodu0083 [package=THT]
  M3 = MAX7219 8x8 single Led Matrix Module
  Grove1 = Grove 4 Digit Display
  RE1 = KY-040 Rotary encoder [package="Breakout board"]
  Деталь4 = Soil Moisture Sensor

nets:
  N1: SensorShield3.pin_136, M3.O-VCC, Деталь4.VCC
  N2: SensorShield3.pin_142, M3.O-GND, Деталь4.GND
  N3: SensorShield3.pin_143, Grove1.GND
  N4: SensorShield3.pin_147, Grove1.VCC
  N5: SensorShield2.pin_136, M2.pin2
  N6: SensorShield2.pin_142, M2.pin3
  N7: SensorShield2.pin_143, RE1.GND
  N8: SensorShield2.pin_147, RE1.Vcc
  N9: SensorShield1.pin_12, U1.pin_44
  N10: SensorShield1.pin_13, U1.pin_43
  N11: SensorShield1.pin_14, U1.pin_42
  N12: SensorShield1.pin_33, U1.pin_37
  N13: SensorShield1.pin_34, U1.pin_36
  N14: SensorShield1.pin_35, U1.pin_35
  N15: SensorShield1.pin_36, U1.pin_38
  N16: SensorShield1.pin_73, U1.pin_31
  N17: SensorShield1.pin_74, U1.pin_30
  N18: SensorShield1.pin_75, U1.pin_29
  N19: SensorShield1.pin_76, U1.pin_28
  N20: SensorShield1.pin_89, U1.pin_27
  N21: SensorShield1.pin_90, U1.pin_26
  N22: SensorShield1.pin_95, U1.pin_24
  N23: SensorShield1.pin_136, LCM1602_IIC1.VCC
  N24: SensorShield1.pin_137, YL-83_-_Control_Board1.VCC
  GND: SensorShield1.pin_142, LCM1602_IIC1.GND, YL-83_-_Control_Board1.GND
  N25: SensorShield1.pin_143, M1.pin_2
  N26: SensorShield1.pin_147, M1.pin_1
  N27: SensorShield1.pin_153, U1.pin_21
  N28: SensorShield1.pin_159, U1.pin_23
  N29: U1.pin_52, Деталь1.D1/TX
  N30: U1.pin_53, Деталь1.VIN
  N31: U1.pin_190, Деталь1.D12/MISO
  N32: U1.pin_191, Деталь1.D13/SCK
  N33: U1.pin_219, Деталь1.D11/MOSI
  N34: U1.pin_220, Деталь1.3V3
  N35: U1.pin_221, Деталь1.D10
  N36: U1.pin_222, Деталь1.AREF
  N37: U1.pin_223, Деталь1.A0
  N38: U1.pin_224, Деталь1.A1
  N39: U1.pin_225, Деталь1.A2
  N40: U1.pin_226, Деталь1.A3
  N41: U1.pin_227, Деталь1.A4
  N42: U1.pin_228, Деталь1.A5
  N43: U1.pin_229, Деталь1.A6
  N44: U1.pin_230, Деталь1.A7
  N45: U1.pin_231, Деталь1.5V
  N46: U1.pin_232, U1.pin_235, Деталь1.RESET
  N47: U1.pin_233, U1.pin_236, Деталь1.GND
  N48: U1.pin_234, Деталь1.D0/RX
  N49: U1.pin_237, Деталь1.D2
  N50: U1.pin_238, Деталь1.D9
  N51: U1.pin_239, Деталь1.D8
  N52: U1.pin_240, Деталь1.D7
  N53: U1.pin_241, Деталь1.D6
  N54: U1.pin_242, Деталь1.D5
  N55: U1.pin_243, Деталь1.D3
  N56: U1.pin_244, Деталь1.D4
  N57: U2.pin_52, Деталь2.D1/TX
  N58: U2.pin_53, Деталь2.VIN
  N59: U2.pin_190, Деталь2.D12/MISO
  N60: U2.pin_191, Деталь2.D13/SCK
  N61: U2.pin_219, Деталь2.D11/MOSI
  N62: U2.pin_220, Деталь2.3V3
  N63: U2.pin_221, Деталь2.D10
  N64: U2.pin_222, Деталь2.AREF
  N65: U2.pin_223, Деталь2.A0
  N66: U2.pin_224, Деталь2.A1
  N67: U2.pin_225, Деталь2.A2
  N68: U2.pin_226, Деталь2.A3
  N69: U2.pin_227, Деталь2.A4
  N70: U2.pin_228, Деталь2.A5
  N71: U2.pin_229, Деталь2.A6
  N72: U2.pin_230, Деталь2.A7
  N73: U2.pin_231, Деталь2.5V
  N74: U2.pin_232, U2.pin_235, Деталь2.RESET
  N75: U2.pin_233, U2.pin_236, Деталь2.GND
  N76: U2.pin_234, Деталь2.D0/RX
  N77: U2.pin_237, Деталь2.D2
  N78: U2.pin_238, Деталь2.D9
  N79: U2.pin_239, Деталь2.D8
  N80: U2.pin_240, Деталь2.D7
  N81: U2.pin_241, Деталь2.D6
  N82: U2.pin_242, Деталь2.D5
  N83: U2.pin_243, Деталь2.D3
  N84: U2.pin_244, Деталь2.D4
  N85: U3.pin_52, Деталь3.D1/TX
  N86: U3.pin_53, Деталь3.VIN
  N87: U3.pin_190, Деталь3.D12/MISO
  N88: U3.pin_191, Деталь3.D13/SCK
  N89: U3.pin_219, Деталь3.D11/MOSI
  N90: U3.pin_220, Деталь3.3V3
  N91: U3.pin_221, Деталь3.D10
  N92: U3.pin_222, Деталь3.AREF
  N93: U3.pin_223, Деталь3.A0
  N94: U3.pin_224, Деталь3.A1
  N95: U3.pin_225, Деталь3.A2
  N96: U3.pin_226, Деталь3.A3
  N97: U3.pin_227, Деталь3.A4
  N98: U3.pin_228, Деталь3.A5
  N99: U3.pin_229, Деталь3.A6
  N100: U3.pin_230, Деталь3.A7
  N101: U3.pin_231, Деталь3.5V
  N102: U3.pin_232, U3.pin_235, Деталь3.RESET
  N103: U3.pin_233, U3.pin_236, Деталь3.GND
  N104: U3.pin_234, Деталь3.D0/RX
  N105: U3.pin_237, Деталь3.D2
  N106: U3.pin_238, Деталь3.D9
  N107: U3.pin_239, Деталь3.D8
  N108: U3.pin_240, Деталь3.D7
  N109: U3.pin_241, Деталь3.D6
  N110: U3.pin_242, Деталь3.D5
  N111: U3.pin_243, Деталь3.D3
  N112: U3.pin_244, Деталь3.D4
  VSS: LCD1.VSS, LCM1602_IIC1.VSS
  VDD: LCD1.VDD, LCM1602_IIC1.VDD
  N113: LCD1.V0, LCM1602_IIC1.V0
  N114: LCD1.RS, LCM1602_IIC1.RS
  N115: LCD1.R/W, LCM1602_IIC1.RW
  N116: LCD1.E, LCM1602_IIC1.E
  N117: LCD1.DB0, LCM1602_IIC1.D0
  N118: LCD1.DB1, LCM1602_IIC1.D1
  N119: LCD1.DB2, LCM1602_IIC1.D2
  N120: LCD1.DB3, LCM1602_IIC1.D3
  N121: LCD1.DB4, LCM1602_IIC1.D4
  N122: LCD1.DB5, LCM1602_IIC1.D5
  N123: LCD1.DB6, LCM1602_IIC1.D6
  N124: LCD1.DB7, LCM1602_IIC1.D7
  N125: LCD1.LED+, LCM1602_IIC1.A
  N126: LCD1.LED-, LCM1602_IIC1.K
  N127: YL-83_-_Control_Board1.POS, YL-83_-_Detection_Board1.POS
  N128: YL-83_-_Control_Board1.NEG, YL-83_-_Detection_Board1.NEG

notes:
  1 - A5 - LCM1602 - SCL
  2 - A4 - LCM1602 - SDA
  3 - D10-MAX7219 - CS
  4 - D11-MAX7219 - CLK
  5 - D12-MAX7219 - DIN
  6 - D9 - Mosfet - TRIG/PWM/SIG
  12 - D3 - Relay - IN
  13 - D4 - TM1637 - CLK
  14 - D5 - TM1637 - DIO
  15 - D17-Encoder - S1 or CLK
  16 - D16-Encoder - S2 or DT
  17 - D15-Encoder - KEY or SW
  18 - A0 - Moisture Sensor - SIG
  26 - A7 - Raindrop - A0

custom parts:
  Duit connection plate: SensorShield
  Sensor_shield_DUIT: Just a shield
  LCD screen 1602: A standard character display, usually with 2x16 characters. Comes in many colors.
  I2C: I2C-Module to use a 1602 or 2004 LCD on with the wire.h libory Serial LCD Modul
  YL-83 Rain Sensor - Control Board: The YL-83 is a rain sensor that has more resistance when dry and less resistance when wet. The module runs at 5V.
  YL-83 Rain Sensor - Detection Board: The YL-83 is a rain sensor that has more resistance when dry and less resistance when wet. The module runs at 5V.
  1 chan 5v relay module: 1 Channel 5V Relay Module Board Shield with Optocoupler Support High and Low Level Trigger for Arduino.
  hcmmodu0083: hcmmodu0083 IRF540 Mosfet driver module
  MAX7219 8x8 single Led Matrix Module: Description: MAX7219 8x8 LedMatrix single Red Module Dimensions: 32x32mm Documents:
  KY-040 Rotary encoder: KY-040 Rotary Encoder with switch on breakout borad from AZ Delivery
